// Logisim project hw_vga_sim.circ as structural Verilog: 1 circuit, main circuit main
module main (
  input  nRST,
  input  nFRAME_END
);

  wire CLK_out, comparator_1_eq, n7411_1_pin2, n74163_1_pin1, n74163_1_pin3, n74163_1_pin7, n74163_1_pin15,
       n74163_2_pin15;
  wire [0:0] n7411_1_pin8;
  wire [11:0] n74163_1_pin14;

  Clock CLK (.out(CLK_out));
  _74163 #(.ShowInternalStructure("true")) u_74163_1 (
    .pin1(n74163_1_pin1), .pin2(CLK_out), .pin3(n74163_1_pin3), .pin4(n74163_1_pin3), .pin5(n74163_1_pin3),
    .pin6(n74163_1_pin3), .pin7(n74163_1_pin7), .pin15(n74163_1_pin15), .pin14(n74163_1_pin14[0]),
    .pin13(n74163_1_pin14[1]), .pin12(n74163_1_pin14[2]), .pin11(n74163_1_pin14[3]), .pin10(n74163_1_pin7),
    .pin9(n74163_1_pin7));
  _7411 #(.ShowInternalStructure("true")) u_7411_1 (
    .pin1(nFRAME_END), .pin2(n7411_1_pin2), .pin13(nRST), .pin12(n74163_1_pin1), .pin11(n74163_1_pin14[0]),
    .pin10(n74163_1_pin14[1]), .pin9(n74163_1_pin14[2]), .pin8(n7411_1_pin8[0]));  // open: pin3, pin4, pin5, pin6
  _74163 #(.ShowInternalStructure("true")) u_74163_2 (
    .pin1(n74163_1_pin1), .pin2(CLK_out), .pin3(n74163_1_pin3), .pin4(n74163_1_pin3), .pin5(n74163_1_pin3),
    .pin6(n74163_1_pin3), .pin7(n74163_1_pin15), .pin15(n74163_2_pin15), .pin14(n74163_1_pin14[4]),
    .pin13(n74163_1_pin14[5]), .pin12(n74163_1_pin14[6]), .pin11(n74163_1_pin14[7]), .pin10(n74163_1_pin15),
    .pin9(n74163_1_pin7));
  Hex_Digit_Display hex_digit_display_1 (.value(n74163_1_pin14[11:8]));  // open: dp
  Hex_Digit_Display hex_digit_display_2 (.value(n74163_1_pin14[7:4]));  // open: dp
  Hex_Digit_Display hex_digit_display_3 (.value(n74163_1_pin14[3:0]));  // open: dp
  _74163 #(.ShowInternalStructure("true")) u_74163_3 (
    .pin1(n74163_1_pin1), .pin2(CLK_out), .pin3(n74163_1_pin3), .pin4(n74163_1_pin3), .pin5(n74163_1_pin3),
    .pin6(n74163_1_pin3), .pin7(n74163_2_pin15), .pin14(n74163_1_pin14[8]), .pin13(n74163_1_pin14[9]),
    .pin12(n74163_1_pin14[10]), .pin11(n74163_1_pin14[11]), .pin10(n74163_2_pin15), .pin9(n74163_1_pin7));  // open: pin15
  not not_1 (n7411_1_pin2, comparator_1_eq);
  Comparator #(.mode("unsigned")) comparator_1 (
    .a({n74163_1_pin14[9:3], n7411_1_pin8[0]}), .b(8'hc7), .eq(comparator_1_eq));  // open: gt, lt
  // also tied to GND on the sheet: n74163_1_pin3
  // also tied to VCC on the sheet: n74163_1_pin7
endmodule
